// Logisim project Processador.circ as structural Verilog: 10 circuits, main circuit main
module main (
  input  reset
);

  wire clk, cpu_1_out_8;
  wire [5:0] cpu_1_out_7;
  wire [7:0] cpu_1_out_5, cpu_1_out_6, ram_1_data, rom_1_data;

  Clock u_clk (.out(clk));
  CPU cpu_1 (
    .in_1(clk), .in_2(rom_1_data), .in_3(reset), .in_4(ram_1_data), .out_5(cpu_1_out_5), .out_6(cpu_1_out_6),
    .out_7(cpu_1_out_7), .out_8(cpu_1_out_8));
  ROM #(.addrWidth(6)) rom_1 (.addr(cpu_1_out_7), .data(rom_1_data));  // open: sel
  RAM #(.bus("separate")) ram_1 (
    .addr(cpu_1_out_6), .din(cpu_1_out_5), .data(ram_1_data), .str(cpu_1_out_8), .clk(clk), .ld(1'b1),
    .clr(reset));  // open: sel

  // Notes on the sheet:
  //   contents of rom_1 (hex, n*v repeats v):
  //   72 63 71 53 80
endmodule

module meiaSoma (
  input  A,
  input  B,
  output C,
  output S
);

  wire and_1_out, and_2_out, not_1_out, not_2_out;

  not not_1 (not_1_out, A);
  not not_2 (not_2_out, B);
  and and_1 (and_1_out, not_1_out, B);
  and and_2 (and_2_out, A, not_2_out);
  or or_1 (S, and_1_out, and_2_out);
  and and_3 (C, A, B);
endmodule

module somaCompleta (
  input  X,
  input  Y,
  input  Z,
  output C,
  output S
);

  wire and_1_out, and_2_out, and_3_out, and_4_out, and_5_out, and_6_out, and_7_out, not_1_out, not_2_out,
       not_3_out;

  not not_1 (not_1_out, X);
  not not_2 (not_2_out, Y);
  not not_3 (not_3_out, Z);
  and and_1 (and_1_out, X, Y, not_3_out);
  and and_2 (and_2_out, X, not_2_out, Z);
  and and_3 (and_3_out, not_1_out, Y, Z);
  and and_4 (and_4_out, X, Y, Z);
  and and_5 (and_5_out, not_1_out, Y, not_3_out);
  and and_6 (and_6_out, not_1_out, not_2_out, Z);
  and and_7 (and_7_out, X, not_2_out, not_3_out);
  or or_1 (C, and_1_out, and_2_out, and_3_out, and_4_out);
  or or_2 (S, and_4_out, and_5_out, and_6_out, and_7_out);
endmodule

module soma (
  input  [3:0] in_1,
  input  [3:0] in_2,
  output [3:0] out_3
);

  wire somacompleta_1_c, somacompleta_2_c, somacompleta_3_c;

  // Probe on in_1
  // Probe on in_2
  somaCompleta somacompleta_1 (.C(somacompleta_1_c), .S(out_3[0]), .X(in_1[0]), .Y(in_2[0]), .Z(1'b0));
  somaCompleta somacompleta_2 (.C(somacompleta_2_c), .S(out_3[1]), .X(somacompleta_1_c), .Y(in_1[1]), .Z(in_2[1]));
  somaCompleta somacompleta_3 (.C(somacompleta_3_c), .S(out_3[2]), .X(somacompleta_2_c), .Y(in_1[2]), .Z(in_2[2]));
  somaCompleta somacompleta_4 (.S(out_3[3]), .X(somacompleta_3_c), .Y(in_1[3]), .Z(in_2[3]));  // open: C
  // Probe on out_3
endmodule

module ULA (
  input  [7:0] A,
  input  [7:0] B,
  input  [1:0] S,
  output [7:0] out_4,
  output out_5
);

  wire [7:0] adder_1_out, and_1_out, multiplier_1_out, or_1_out;

  Adder adder_1 (.a(A), .b(B), .out(adder_1_out));  // open: cin, cout
  Multiplier multiplier_1 (.a(A), .b(B), .out(multiplier_1_out));  // open: cin, cout
  assign and_1_out = A & B;  // AND_Gate and_1, 8 bits wide
  assign or_1_out = A | B;  // OR_Gate or_1, 8 bits wide
  Multiplexer #(.select(2), .width(8)) multiplexer_1 (
    .in0(adder_1_out), .in1(multiplier_1_out), .in2(and_1_out), .in3(or_1_out), .out(out_4), .sel(S));  // open: en
  Comparator #(.mode("unsigned")) comparator_1 (.a(A), .b(B), .gt(out_5));  // open: eq, lt
endmodule

module Latch (
  input  in_1,
  input  in_2,
  output out_3
);

  wire and_1_out, and_2_out, not_1_out, not_2_out, not_4_out;

  not not_1 (not_1_out, in_1);
  and and_1 (and_1_out, not_1_out, not_4_out);
  and and_2 (and_2_out, out_3, not_2_out);
  not not_2 (not_2_out, in_2);
  not not_3 (out_3, and_1_out);
  not not_4 (not_4_out, and_2_out);
endmodule

module FlipFlop (
  input  \input ,
  input  clk,
  input  en,
  input  reset,
  output out_5
);

  wire and_1_out, and_2_out, and_3_out, not_1_out, or_1_out;

  not not_1 (not_1_out, \input );
  and and_1 (and_1_out, clk, en);
  and and_2 (and_2_out, \input , and_1_out);
  and and_3 (and_3_out, and_1_out, not_1_out);
  or or_1 (or_1_out, and_3_out, reset);
  Latch latch_1 (.in_1(and_2_out), .in_2(or_1_out), .out_3(out_5));
endmodule

module register (
  input  clk,
  input  \input ,
  input  en,
  input  reset,
  output out_5
);

  wire flipflop_1_out_5, not_1_out;

  not not_1 (not_1_out, clk);
  FlipFlop flipflop_1 (.\input (\input ), .clk(clk), .en(en), .reset(reset), .out_5(flipflop_1_out_5));
  FlipFlop flipflop_2 (.\input (flipflop_1_out_5), .clk(not_1_out), .en(en), .reset(reset), .out_5(out_5));
endmodule

module REGS (
  input  [1:0] addA,
  input  [1:0] addB,
  input  [7:0] Input,
  input  clk,
  input  reset,
  input  en,
  output [7:0] outA,
  output [7:0] outB
);

  wire en0, en1, en2, en3;
  wire [7:0] q0, q1, q2, q3;

  Register register_1 (.D(Input), .en(en0), .Q(q0), .clk(clk), .clr(reset));
  Register register_2 (.D(Input), .en(en2), .Q(q2), .clk(clk), .clr(reset));
  Demultiplexer #(.select(2)) demultiplexer_1 (
    .out0(en0), .out1(en1), .out2(en2), .out3(en3), .in(en), .sel(addA));  // open: en
  Register register_3 (.D(Input), .en(en1), .Q(q1), .clk(clk), .clr(reset));
  Register register_4 (.D(Input), .en(en3), .Q(q3), .clk(clk), .clr(reset));
  Multiplexer #(.select(2), .width(8)) multiplexer_1 (
    .in0(q0), .in1(q1), .in2(q2), .in3(q3), .out(outA), .sel(addA));  // open: en
  Multiplexer #(.select(2), .width(8)) multiplexer_2 (
    .in0(q0), .in1(q1), .in2(q2), .in3(q3), .out(outB), .sel(addB));  // open: en
endmodule

module CPU (
  input  in_1,
  input  [7:0] in_2,
  input  in_3,
  input  [7:0] in_4,
  output [7:0] out_5,
  output [7:0] out_6,
  output [5:0] out_7,
  output out_8
);

  wire cmp, goJg, isAdd, isAnd, isCmp, isJg, isMov, isMul, isOr, isSpecialCase, movecons, not_1_out,
       not_2_out, not_3_out, not_4_out, not_5_out, not_6_out, not_7_out, not_8_out, not_9_out, not_10_out,
       not_11_out, not_12_out, not_13_out, not_14_out, not_15_out, not_16_out, not_17_out, not_18_out,
       not_19_out, regen, ula_1_out_5;
  wire [1:0] multiplexer_3_out, op;
  wire [5:0] adder_1_out, nextline;
  wire [7:0] multiplexer_1_out, multiplexer_2_out, outB, outULA, regs_1_outa;

  not not_1 (not_1_out, in_2[6]);
  not not_2 (not_2_out, in_2[5]);
  and and_1 (isCmp, in_2[4], not_2_out, in_2[6], not_3_out);
  not not_3 (not_3_out, in_2[7]);
  and and_2 (goJg, isJg, cmp);
  and and_3 (isJg, not_1_out, in_2[7]);
  Multiplexer #(.width(8)) multiplexer_1 (
    .in0(outULA), .in1({{6{1'b0}}, in_2[1:0]}), .out(multiplexer_1_out), .sel(movecons));  // open: en
  Register #(.width(6)) register_1 (.D(nextline), .en(in_1), .Q(out_7), .clk(in_1), .clr(in_3));
  Multiplexer #(.width(8)) multiplexer_2 (
    .in0(multiplexer_1_out), .in1(outB), .out(multiplexer_2_out), .sel(isMov));  // open: en
  not not_4 (not_4_out, in_2[4]);
  not not_5 (not_5_out, in_2[7]);
  Multiplexer #(.width(2)) multiplexer_3 (
    .in0(in_2[3:2]), .in1(2'b11), .out(multiplexer_3_out), .sel(isSpecialCase));  // open: en
  and and_4 (isMov, not_4_out, in_2[5], in_2[6], not_5_out);
  Adder #(.width(6)) adder_1 (.a(out_7), .b(6'b000001), .out(adder_1_out));  // open: cin, cout
  Subtractor #(.width(2)) subtractor_1 (.a(in_2[5:4]), .b(2'b01), .out(op));  // open: bin, bout
  Multiplexer #(.width(6)) multiplexer_4 (.in0(adder_1_out), .in1(in_2[5:0]), .out(nextline), .sel(goJg));  // open: en
  REGS regs_1 (
    .addA(multiplexer_3_out), .addB(in_2[1:0]), .Input(multiplexer_2_out), .clk(in_1), .reset(in_3),
    .en(regen), .outA(regs_1_outa), .outB(outB));
  not not_6 (not_6_out, in_2[5]);
  not not_7 (not_7_out, in_2[6]);
  not not_8 (not_8_out, in_2[7]);
  not not_9 (not_9_out, in_2[4]);
  and and_5 (isMul, not_9_out, in_2[5], not_10_out, not_11_out);
  not not_10 (not_10_out, in_2[6]);
  not not_11 (not_11_out, in_2[7]);
  not not_12 (not_12_out, in_2[6]);
  not not_13 (not_13_out, in_2[7]);
  not not_14 (not_14_out, in_2[4]);
  not not_15 (not_15_out, in_2[5]);
  not not_16 (not_16_out, in_2[7]);
  ULA ula_1 (.A(regs_1_outa), .B(outB), .S(op), .out_4(outULA), .out_5(ula_1_out_5));
  and and_6 (isAdd, in_2[4], not_6_out, not_7_out, not_8_out);
  and and_7 (isAnd, in_2[4], in_2[5], not_12_out, not_13_out);
  and and_8 (isOr, not_14_out, not_15_out, in_2[6], not_16_out);
  Register #(.width(1)) register_2 (.D(ula_1_out_5), .en(isCmp), .Q(cmp), .clk(in_1), .clr(in_3));
  not not_17 (not_17_out, in_2[2]);
  not not_18 (not_18_out, in_2[3]);
  and and_9 (movecons, not_17_out, not_18_out, in_2[4], in_2[5], in_2[6], not_19_out);
  not not_19 (not_19_out, in_2[7]);
  or or_1 (regen, isAnd, isAdd, isMul, isOr, movecons, isMov);
  buf or_2 (isSpecialCase, movecons);  // OR_Gate

  // Other names for the same wires on the sheet: lineLg[5:0] = in_2[5:0]; opcode[7:0] = in_2; addA[1:0] = in_2[3:2];
  //   clk = in_1; addB[1:0] = in_2[1:0]; constant[1:0] = in_2[1:0]; memoryadd[7:0] = out_6; memoryin[7:0] = out_5;
  //   memoryout[7:0] = in_4; PC[5:0] = out_7; reset = in_3; str = out_8
endmodule
